# Fritzing sketch sketch (saved by Fritzing 0.9.9b)
breadboards: 1

parts:
  Part1 = Arduino Uno (Rev3)
  IR_Reader = TSOP312.., 314.. [package=THT]

nets:
  N1: Part1.D2, IR_Reader.Data
  N2: Part1.5V, IR_Reader.Vs
  GND: Part1.GND, IR_Reader.GND
